# Fritzing sketch mute button sketch (saved by Fritzing 0.9.4)
breadboards: 1

parts:
  Part1 = Adafruit MCP2221A USB to GPIO / ADC / DAC breakout [part_number="Adafruit #4471"]  # not connected
  S1 = Pushbutton [package="[SMD]"]
  R1 = Resistor [tolerance=±5% resistance=10k package="2512 [SMD]"]

nets:
  N1: S1.Pin_1, S1.Pin_2
  N2: S1.Pin_3, S1.Pin_4, R1.Pin_0

custom parts:
  Adafruit MCP2221A USB to GPIO / ADC / DAC breakout: Wouldn't it be cool to drive a tiny OLED display, read a color sensor, or even just flash some LEDs directly from your computer? Sure you can program an Arduino or Trinket to talk to these devices and your computer, but why can't your computer just talk to those devices and sensors itself? Well, now your computer can talk to devices using the Adafruit MCP2221A breakout board!
